// Digital circuit alu.dig as structural Verilog
module alu (
  input  [63:0] dec_op,
  input  [31:0] val_r1,
  input  [31:0] val_pc,
  input  [31:0] val_r2,
  input  reg2_en,
  input  [31:0] val_imm,
  input  en,
  output [31:0] out
);

  wire add, addsub, \and , auipc, lui, not_1_out, not_2_out, \or , or_1_out, r_type, sll, slt, sltu, sra,
       srl, srla, sub, u_type, \xor ;
  wire [0:0] comparator_1_lt, comparator_2_lt;
  wire [7:0] driver_2_out, func3, func7;
  wire [11:0] decoder_output_decoder_1_flags;
  wire [31:0] add_1_s, and_5_out, input_1, input_2, or_2_out, result, sll_out, sra_out, srl_out, sub_1_s,
       xor_1_out;

  PullDown #(.Bits(32)) pulldown_1 (.out(val_r1));
  PullDown #(.Bits(32)) pulldown_2 (.out(val_pc));
  PullDown #(.Bits(32)) pulldown_3 (.out(val_r2));
  PullDown pulldown_4 (.out(reg2_en));
  decoder_output_decoder decoder_output_decoder_1 (
    .dec_op(dec_op), .func3(func3), .func7(func7), .flags(decoder_output_decoder_1_flags));  // open: opcode, rd1, rs1, rs2
  // decoder_flag_decoder decoder_flag_decoder_1: pin names not known; wires that end beside it: decoder_output_decoder_1_flags, r_type, u_type, auipc, lui
  assign out = en ? result : 32'bz;  // Driver driver_1
  PullDown #(.Bits(32)) pulldown_5 (.out(out));
  Multiplexer #(.Bits(32)) multiplexer_1 (.sel(auipc), .in_0(val_r1), .in_1(val_pc), .out(input_1));
  Multiplexer #(.Bits(32)) multiplexer_2 (.sel(reg2_en), .in_0(val_imm), .in_1(val_r2), .out(input_2));
  not not_1 (not_1_out, u_type);
  and and_1 (srl, srla, ~func7[5]);  // And
  assign driver_2_out = not_1_out ? func3 : 8'bz;  // Driver driver_2
  and and_2 (sra, srla, func7[5]);
  and and_3 (sub, r_type, func7[5], addsub);
  PullDown #(.Bits(8)) pulldown_6 (.out(driver_2_out));
  Decoder #(.Selector_Bits(3)) decoder_1 (
    .sel(driver_2_out[2:0]), .out_0(addsub), .out_1(sll), .out_2(slt), .out_3(sltu), .out_4(\xor ),
    .out_5(srla), .out_6(\or ), .out_7(\and ));
  and and_4 (add, ~sub, not_2_out, addsub);  // And
  not not_2 (not_2_out, u_type);
  or or_1 (or_1_out, auipc, add);
  Add #(.Bits(32)) add_1 (.a(input_1), .b(input_2), .c_i(1'b0), .s(add_1_s));  // open: c_o
  Sub #(.Bits(32)) sub_1 (.a(input_1), .b(input_2), .c_i(1'b0), .s(sub_1_s));  // open: c_o
  BarrelShifter #(.Bits(32)) u_sll (.in(input_1), .shift(input_2[5:0]), .out(sll_out));
  BarrelShifter #(.Bits(32), .direction("right")) u_srl (.in(input_1), .shift(input_2[5:0]), .out(srl_out));
  BarrelShifter #(.barrelShifterMode("arithmetic"), .Bits(32), .barrelSigned("true"), .direction("right")) u_sra (
    .in(input_1), .shift(input_2[6:0]), .out(sra_out));
  assign result = or_1_out ? add_1_s : 32'bz;  // Driver driver_3
  assign result = sub ? sub_1_s : 32'bz;  // Driver driver_4
  assign result = sll ? sll_out : 32'bz;  // Driver driver_5
  assign result = srl ? srl_out : 32'bz;  // Driver driver_6
  assign result = sra ? sra_out : 32'bz;  // Driver driver_7
  assign result = lui ? val_imm : 32'bz;  // Driver driver_8
  assign xor_1_out = input_1 ^ input_2;  // XOr xor_1, 32 bits wide
  assign or_2_out = input_1 | input_2;  // Or or_2, 32 bits wide
  assign and_5_out = input_1 & input_2;  // And and_5, 32 bits wide
  Comparator #(.Bits(32)) comparator_1 (.a(input_1), .b(input_2), .lt(comparator_1_lt[0]));  // open: gt, eq
  Comparator #(.Signed("true"), .Bits(32)) comparator_2 (
    .a(input_1), .b(input_2), .lt(comparator_2_lt[0]));  // open: gt, eq
  assign result = \xor  ? xor_1_out : 32'bz;  // Driver driver_9
  assign result = \or  ? or_2_out : 32'bz;  // Driver driver_10
  assign result = \and  ? and_5_out : 32'bz;  // Driver driver_11
  assign result = sltu ? {{31{1'b0}}, comparator_1_lt[0]} : 32'bz;  // Driver driver_12
  assign result = slt ? {{31{1'b0}}, comparator_2_lt[0]} : 32'bz;  // Driver driver_13

  // Other names for the same wires on the sheet: en_flag = en; func7_flag = func7[5]

  // Notes on the sheet:
  //   I/O Decode
  //   Function Decode
  //   Operations
endmodule

/* Test case:
val_r1      val_r2 reg2_en en dec_op             out
# add
   5        5      1       1  (0x0000000000000000+(0b000010000000<<48)) 10

# sub
   5        5      1       1  (0x0000200000000000+(0b000010000100<<48))   0

# sll
   1        1      1       1  0x0000000000010000 2

# srl
   2        1      1       1  0x0000000000050000 1
0x80000003  1      1       1  0x0000000000050000 0x40000001

# sra
0xffffffff  1      1       1  0x0000200000050000 0xffffffff
0x80000001  1      1       1  0x0000200000050000 0xC0000000
*/
