// Digital circuit branch.dig as structural Verilog
module branch (
  input  [63:0] dec_op,
  input  branch_en,
  input  [31:0] val_pc,
  input  [31:0] val_r1,
  input  [31:0] val_imm,
  input  [31:0] val_r2,
  input  branch_cond,
  input  branch_jalr,
  output [31:0] val_out,
  output [31:0] sp_addr,
  output sp_en
);

  wire beq, bge, bgeu, blt, bne, driver_1_out, gltu, multiplexer_2_out, not_1_out, or_1_out, or_2_out,
       pulldown_1_out, pulldown_2_out, signed_eq, signed_gt, signed_lt, unsigned_eq, unsigned_gt, unsigned_lt;
  wire [7:0] func3;
  wire [31:0] add_1_s, add_2_s, and_1_out, multiplexer_1_out;

  // decoder_output_decoder decoder_output_decoder_1: pin names not known; wires that end beside it: dec_op, func3
  Decoder #(.Selector_Bits(3)) decoder_1 (
    .sel(func3[2:0]), .out_0(beq), .out_1(bne), .out_3(blt), .out_5(bge), .out_6(gltu), .out_7(bgeu));  // open: out_2, out_4
  Multiplexer #(.Bits(32)) multiplexer_1 (.sel(branch_jalr), .in_0(val_pc), .in_1(val_r1), .out(multiplexer_1_out));
  Add #(.Bits(32)) add_1 (.a(multiplexer_1_out), .b(val_imm), .c_i(pulldown_1_out), .s(add_1_s));  // open: c_o
  PullDown pulldown_1 (.out(pulldown_1_out));
  Comparator #(.Signed("true"), .Bits(32)) \signed  (
    .a(val_r1), .b(val_r2), .gt(signed_gt), .eq(signed_eq), .lt(signed_lt));
  Comparator #(.Bits(32)) \unsigned  (.a(val_r1), .b(val_r2), .gt(unsigned_gt), .eq(unsigned_eq), .lt(unsigned_lt));
  or or_1 (or_1_out, signed_gt, signed_eq);
  or or_2 (or_2_out, unsigned_gt, unsigned_eq);
  Add #(.Bits(32)) add_2 (.a(val_pc), .b(32'h4), .c_i(pulldown_2_out), .s(add_2_s));  // open: c_o
  PullDown pulldown_2 (.out(pulldown_2_out));
  assign and_1_out = add_1_s & 32'hfffffffe;  // And and_1, 32 bits wide
  not not_1 (not_1_out, signed_eq);
  assign driver_1_out = bge ? or_1_out : 1'bz;  // Driver driver_1
  assign driver_1_out = beq ? signed_eq : 1'bz;  // Driver driver_2
  assign driver_1_out = bne ? not_1_out : 1'bz;  // Driver driver_3
  assign driver_1_out = blt ? signed_lt : 1'bz;  // Driver driver_4
  assign driver_1_out = bgeu ? or_2_out : 1'bz;  // Driver driver_5
  assign driver_1_out = gltu ? unsigned_lt : 1'bz;  // Driver driver_6
  assign val_out = branch_en ? add_2_s : 32'bz;  // Driver driver_7
  assign sp_addr = branch_en ? and_1_out : 32'bz;  // Driver driver_8
  PullDown #(.Bits(32)) pulldown_3 (.out(sp_addr));
  Multiplexer multiplexer_2 (.sel(branch_cond), .in_0(1'b1), .in_1(driver_1_out), .out(multiplexer_2_out));
  assign sp_en = branch_en ? multiplexer_2_out : 1'bz;  // Driver driver_9
  PullDown pulldown_4 (.out(sp_en));
endmodule
