// Digital circuit controller.dig as structural Verilog
module controller (
  input  [63:0] dec_op,
  input  clk,
  output reg_1,
  output pc_1,
  output reg_2,
  output imm_2,
  output alu_en,
  output rs_en,
  output pc_en,
  output mem_en,
  output mem_save,
  output branch_en,
  output branch_cond,
  output branch_jalr,
  output pip_fetch,
  output pip_exec,
  output pip_write
);

  wire and_2_out, and_3_out, arth_type, auipc, comparator_5_gt, comparator_5_lt, j_type, jal, jump,
       load_type, mem_rdy, or_1_out, r_type, u_type;
  wire [2:0] add_1_s, delay, pip_cnt_out;
  wire [7:0] func3, opcode;
  wire [11:0] decoder_output_decoder_1_flags;

  decoder_output_decoder decoder_output_decoder_1 (
    .dec_op(dec_op), .opcode(opcode), .func3(func3), .flags(decoder_output_decoder_1_flags));  // open: rd1, rs1, rs2, func7
  // decoder_flag_decoder decoder_flag_decoder_1: pin names not known; wires that end beside it: decoder_output_decoder_1_flags, mem_save, r_type, u_type, j_type, load_type, arth_type, auipc
  Counter #(.Bits(3)) pip_cnt (.en(1'b1), .C(clk), .clr(mem_rdy), .out(pip_cnt_out));  // open: ovf
  or or_1 (or_1_out, r_type, arth_type, u_type, load_type, jump);
  Comparator #(.Bits(8)) comparator_1 (.a(8'h6f), .b(opcode), .eq(jal));  // open: gt, lt
  Comparator #(.Bits(8)) comparator_2 (.a(8'h63), .b(opcode), .eq(branch_cond));  // open: gt, lt
  Comparator #(.Bits(8)) comparator_3 (.a(8'h67), .b(opcode), .eq(branch_jalr));  // open: gt, lt
  Add #(.Bits(3)) add_1 (.a(func3[2:0]), .b(3'b001), .c_i(1'b0), .s(add_1_s));  // open: c_o
  or or_2 (reg_2, r_type, branch_cond, mem_save);
  or or_3 (imm_2, arth_type, 1'b0);
  or or_4 (branch_en, jal, branch_cond, branch_jalr);
  or or_5 (jump, jal, branch_jalr);
  Multiplexer #(.Bits(3)) multiplexer_1 (.sel(mem_en), .in_0(3'b000), .in_1(add_1_s), .out(delay));
  or or_6 (reg_1, r_type, arth_type, mem_save, load_type, branch_cond, branch_jalr);
  or or_7 (alu_en, r_type, arth_type, u_type);
  Comparator #(.Bits(3)) comparator_4 (.a(3'b000), .b(pip_cnt_out), .eq(pip_fetch));  // open: gt, lt
  Comparator #(.Bits(3)) comparator_5 (
    .a(delay), .b(pip_cnt_out), .gt(comparator_5_gt), .eq(pc_en), .lt(comparator_5_lt));
  or or_8 (mem_en, mem_save, load_type);
  and and_1 (rs_en, or_1_out, pc_en);
  and and_2 (and_2_out, ~pip_fetch, comparator_5_gt);  // And
  and and_3 (and_3_out, pip_fetch, pc_en);
  or or_9 (mem_rdy, pc_en, comparator_5_lt);
  or or_10 (pip_exec, and_2_out, and_3_out);

  assign pc_1 = 1'b0;
  assign pip_write = pc_en;

  // Other names for the same wires on the sheet: branch = branch_en; cond = branch_cond; exec = pip_exec;
  //   fetch = pip_fetch; jalr = branch_jalr; reg_save = rs_en; s_type = mem_save; write = pc_en

  // Notes on the sheet:
  //   JAL
  //   COND
  //   JALR
endmodule

/* Test case:
dec_op           pc_en branch_en branch_cond branch_jalr
0x02000802020823 0     0         0           0
0x2014040000016F 1     1         0           0
0x20140400000167 1     1         0           1
0x20140400000163 1     1         1           0
*/
