// Digital circuit decoder-output-decoder.dig as structural Verilog
module decoder_output_decoder (
  input  [63:0] dec_op,
  output [7:0] opcode,
  output [7:0] rd1,
  output [7:0] func3,
  output [7:0] rs1,
  output [7:0] rs2,
  output [7:0] func7,
  output [11:0] flags
);


  assign flags = dec_op[59:48];
  assign func3 = dec_op[23:16];
  assign func7 = dec_op[47:40];
  assign opcode = dec_op[7:0];
  assign rd1 = dec_op[15:8];
  assign rs1 = dec_op[31:24];
  assign rs2 = dec_op[39:32];

  // Notes on the sheet:
  //   dec_op: Bus with all the type flags
endmodule
