// Digital circuit main.dig as structural Verilog
module main (
  input  clk
);

  // riscv riscv_1: pin names not known; wires that end beside it: clk

  // Notes on the sheet:
  //   clk: Hz: 10
endmodule
