// Digital circuit pc.dig as structural Verilog
module pc (
  input  [31:0] sp_addr,
  input  write_enf,
  input  pc_en,
  input  clk,
  output [31:0] val_pc
);

  wire pulldown_1_out, pullup_1_out;
  wire [31:0] add_1_s, multiplexer_1_out, multiplexer_2_out;

  PullDown pulldown_1 (.out(pulldown_1_out));
  Register #(.Bits(32)) register_1 (.D(multiplexer_2_out), .C(clk), .en(pullup_1_out), .Q(val_pc));
  Add #(.Bits(32)) add_1 (.a(val_pc), .b(32'h4), .c_i(pulldown_1_out), .s(add_1_s));  // open: c_o
  PullUp pullup_1 (.out(pullup_1_out));
  Multiplexer #(.Bits(32)) multiplexer_1 (.sel(pc_en), .in_0(val_pc), .in_1(add_1_s), .out(multiplexer_1_out));
  Multiplexer #(.Bits(32)) multiplexer_2 (
    .sel(write_enf), .in_0(multiplexer_1_out), .in_1(sp_addr), .out(multiplexer_2_out));

  // Other names for the same wires on the sheet: sp_en = write_enf
endmodule
