// Digital circuit register-file-simple.dig as structural Verilog
module register_file_simple (
  input  clk,
  input  [7:0] SS,
  input  [7:0] LS_1,
  input  [7:0] LS_2,
  input  [31:0] data,
  input  en_s2,
  input  en_l1,
  input  en_l2,
  output [31:0] out_1,
  output [31:0] out_2
);

  wire comparator_1_eq, comparator_2_eq;
  wire [31:0] multiplexer_1_out, multiplexer_2_out, registerfile_1_da, registerfile_1_db;

  RegisterFile #(.AddrBits(5), .Bits(32)) registerfile_1 (
    .Din(data), .we(en_s2), .Rw(SS[4:0]), .C(clk), .Ra(LS_1[4:0]), .Rb(LS_2[4:0]), .Da(registerfile_1_da),
    .Db(registerfile_1_db));
  Comparator #(.Bits(8)) comparator_1 (.a(LS_1), .b({8{1'b0}}), .eq(comparator_1_eq));  // open: gt, lt
  Comparator #(.Bits(8)) comparator_2 (.a(LS_2), .b({8{1'b0}}), .eq(comparator_2_eq));  // open: gt, lt
  Multiplexer #(.Bits(32)) multiplexer_1 (
    .sel(comparator_1_eq), .in_0(registerfile_1_da), .in_1({32{1'b0}}), .out(multiplexer_1_out));
  Multiplexer #(.Bits(32)) multiplexer_2 (
    .sel(comparator_2_eq), .in_0(registerfile_1_db), .in_1({32{1'b0}}), .out(multiplexer_2_out));
  assign out_1 = en_l1 ? multiplexer_1_out : 32'bz;  // Driver driver_1
  PullDown #(.Bits(32)) pulldown_1 (.out(out_1));
  assign out_2 = en_l2 ? multiplexer_2_out : 32'bz;  // Driver driver_2
  PullDown #(.Bits(32)) pulldown_2 (.out(out_2));

  // Notes on the sheet:
  //   SS: Load Select 1
  //   LS_1: Load Select 1
endmodule
